// Digital circuit soc.dig as structural Verilog
module soc (
  input  rst_n,
  input  clk,
  input  [7:0] uio_in,
  input  [7:0] ui_in,
  output [7:0] uo_out,
  output [7:0] uio_out,
  output [7:0] uio_oe
);

  wire and_1_out, clk_p, cs_flash, memory_controller_1_data_ready, nna8v2_mpu_mux_1_r, nna8v2_mpu_mux_1_w,
       rst, rw;
  wire [7:0] data_in, data_out;
  wire [15:0] addr_out;

  // Probe on ui_in
  not not_1 (rst, rst_n);
  not not_2 (uio_out[0], cs_flash);
  not not_3 (uio_out[6], 1'b0);
  not not_4 (uio_out[7], 1'b0);
  nna8v2_mpu_mux nna8v2_mpu_mux_1 (
    .clk(clk_p), .data_in(data_in), .rst(rst), .addr_out(addr_out), .data_out(data_out),
    .r(nna8v2_mpu_mux_1_r), .w(nna8v2_mpu_mux_1_w));  // open: brk
  memory_controller memory_controller_1 (
    .clk(clk), .addr_in(addr_out), .SPI_in({uio_in[5:4], uio_in[2:1]}), .rst(rst), .data_in(data_out),
    .write(nna8v2_mpu_mux_1_w), .data_out(data_in), .data_ready(memory_controller_1_data_ready),
    .SPI_out({uio_out[5:4], uio_out[2:1]}), .SPI_oe(uio_oe[5]), .SPI_cs(cs_flash));
  or or_1 (rw, nna8v2_mpu_mux_1_r, nna8v2_mpu_mux_1_w);
  and and_1 (and_1_out, clk, ~rw);  // And
  or or_2 (clk_p, and_1_out, memory_controller_1_data_ready);

  assign {uio_oe[7:6], uio_oe[4:0]} = {2'b11, uio_oe[5], 1'b1, {2{uio_oe[5]}}, 1'b1};
  assign uio_out[3] = clk;
  assign uo_out = {8{1'b0}};

  // Other names for the same wires on the sheet: sd0_oe = uio_oe[5]; sd1_oe = uio_oe[5]; sd2_oe = uio_oe[5];
  //   sd3_oe = uio_oe[5]; spi_oe[3:0] = {4{uio_oe[5]}}; clk_spi = clk; sd0_out = uio_out[1];
  //   spi_out[3:0] = {uio_out[5:4], uio_out[2:1]}; sd1_out = uio_out[2]; sd2_out = uio_out[4]; sd3_out = uio_out[5];
  //   sd0_in = uio_in[1]; spi_in[3:0] = {uio_in[5:4], uio_in[2:1]}; sd1_in = uio_in[2]; sd2_in = uio_in[4];
  //   sd3_in = uio_in[5]

  // Notes on the sheet:
  //   spi pin maps
endmodule
